# Fritzing sketch Circuit Éléctrique (saved by Fritzing 0.9.3b)
breadboards: 1

parts:
  MPU-1 = Adafruit MPU6050
  Composant1 = 24 NeoPixel Ring [part_number=1586]
  IC1 = L293D [package=THT]
  M2 = DC Motor
  Composant2 = Arduino Uno (Rev3)
  M1 = DC Motor
  VCC1 = Battery
  S1 = Round Pushbutton
  J1 = Basic Servo
  J2 = Basic Servo
  J3 = Basic Servo

nets:
  GND: MPU-1.GND, Composant1.OUT, IC1.In_4, Composant2.GND, VCC1.-, J1.gnd, J2.gnd, J3.gnd
  VCC: MPU-1.VCC, Composant2.5V, J1.vcc, J2.vcc, J3.vcc
  N1: MPU-1.SDA, Composant2.A4/SDA
  N2: MPU-1.SCL, Composant2.A5/SCL
  N3: Composant1.IN, IC1.+V, Composant2.VIN, S1.leg1
  N4: Composant1.GND, Composant2.D6_PWM
  N5: IC1.Out_1_(_Controlled_by_Enable_1_), IC1.0V, Composant2.D2, Composant2.D3_PWM, M1.pin_1, M1.pin_2
  N6: IC1.Out_2_(_Controlled_by_Enable_1_), IC1.In_2, M2.pin_1, M2.pin_2
  N7: IC1.In_3, Composant2.D7
  N8: IC1.Out_3_(_Controlled_by_Enable_2_), Composant2.D4
  N9: Composant2.D9_PWM, J2.pulse
  N10: Composant2.D10_PWM/SS, J1.pulse
  N11: Composant2.D12/MISO, J3.pulse
  N12: VCC1.+, S1.leg0

custom parts:
  Adafruit MPU6050: The MPU-6050 is a popular six axis accelerometer and gyroscope (gyro) that has all the info you need on how things are shakin' and spinnin' . With six axes of sensing and 16-bit measurements, you'll have everything you need to give your robot friend an inner ear. This combination of gyroscopes and accelerometers is commonly referred to as an Inertial Measurement Unit or IMU. Not so long ago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
  24 NeoPixel Ring: 24 ultra bright smart LED NeoPixels are arranged in a circle with 2.6" (66mm) outer diameter. The rings are 'chainable' - connect the output pin of one to the input pin of another. Use only one microcontroller pin to control as many as you can chain together! Each LED is addressable as the driver chip is inside the LED. Each one has ~18mA constant current drive so the color will be very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
